// Logisim project Group_7_Part_3.circ as structural Verilog: 1 circuit, main circuit part3
module part3 (
  input  A,
  input  B,
  input  C,
  input  D,
  output out_5,
  output out_6,
  output out_7,
  output out_8,
  output out_9,
  output out_10,
  output out_11
);

  wire and_1_out, and_2_out, and_3_out, and_4_out, and_5_out, and_6_out, and_7_out, and_8_out, and_9_out,
       and_10_out, and_11_out, and_12_out, and_13_out, and_14_out, and_15_out, and_16_out, and_17_out,
       not_1_out, not_2_out, not_3_out, not_4_out;

  not not_1 (not_1_out, A);
  not not_2 (not_2_out, B);
  not not_3 (not_3_out, C);
  not not_4 (not_4_out, D);
  and and_1 (and_1_out, not_1_out, C);
  and and_2 (and_2_out, not_1_out, B, D);
  and and_3 (and_3_out, A, not_2_out, not_3_out);
  and and_4 (and_4_out, not_2_out, not_3_out, not_4_out);
  and and_5 (and_5_out, not_1_out, not_2_out);
  and and_6 (and_6_out, not_1_out, not_3_out, not_4_out);
  and and_7 (and_7_out, not_1_out, C, D);
  and and_8 (and_8_out, A, not_2_out, not_3_out);
  and and_9 (and_9_out, not_1_out, B);
  and and_10 (and_10_out, not_1_out, D);
  and and_11 (and_11_out, A, not_2_out, not_3_out);
  and and_12 (and_12_out, not_2_out, not_3_out, not_4_out);
  and and_13 (and_13_out, not_1_out, not_2_out, C);
  and and_14 (and_14_out, not_1_out, C, not_4_out);
  and and_15 (and_15_out, not_1_out, B, not_3_out, D);
  and and_16 (and_16_out, not_1_out, B, not_3_out);
  and and_17 (and_17_out, not_1_out, B, not_4_out);
  or a1 (out_5, and_1_out, and_2_out, and_3_out, and_4_out);
  or b_1 (out_6, and_5_out, and_6_out, and_7_out, and_8_out);
  or c_1 (out_7, and_9_out, and_10_out, and_11_out, and_12_out);
  or d_1 (out_8, and_13_out, and_14_out, and_11_out, and_12_out, and_15_out);
  or e (out_9, and_12_out, and_14_out);
  or f (out_10, and_3_out, and_6_out, and_16_out, and_17_out);
  or g (out_11, and_13_out, and_3_out, and_17_out, and_14_out);
  _7_Segment_Display u_7_segment_display_1 (
    .g(out_11), .f(out_10), .a(out_5), .b(out_6), .e(out_9), .d(out_8), .c(out_7));  // open: dp

  // Notes on the sheet:
  //   A'C
  //   A'BD
endmodule
