// Logisim project Group_7_Project1.circ as structural Verilog: 2 circuits, main circuit clock_work
module clock_work (
  input  set_minutes,
  input  set_hours,
  input  set_alarm,
  input  [1:0] select_inputs,
  output [3:0] seconds_1,
  output [3:0] seconds_0,
  output alarm_signal,
  output [15:0] output_time
);

  wire and_1_out, and_2_out, clock_1_out, comparator_1_eq, comparator_3_eq, counter_1_carry, counter_2_carry,
       counter_3_carry, counter_4_carry, counter_5_carry, counter_6_carry, counter_7_carry, counter_8_carry,
       counter_9_carry, counter_10_carry, or_1_out, or_2_out;
  wire [3:0] counter_5_q, counter_6_q, counter_7_q, counter_8_q, counter_9_q, counter_10_q, register_1_q,
       register_2_q;
  wire [7:0] register_3_q;
  wire [15:8] counter_3_q;

  Clock clock_1 (.out(clock_1_out));
  Counter #(.max('h6), .width(4)) counter_1 (
    .clr(counter_1_carry), .clk(counter_2_carry), .carry(counter_1_carry), .Q(seconds_1));  // open: load, up, count, D
  Counter #(.max('ha), .width(4)) counter_2 (
    .clr(counter_2_carry), .clk(clock_1_out), .carry(counter_2_carry), .Q(seconds_0));  // open: load, up, count, D
  Counter #(.max('h6), .width(4)) counter_3 (
    .clr(counter_3_carry), .clk(counter_4_carry), .carry(counter_3_carry), .Q(counter_3_q[11:8]));  // open: load, up, count, D
  Counter #(.max('ha), .width(4)) counter_4 (
    .clr(counter_4_carry), .clk(counter_1_carry), .carry(counter_4_carry), .Q(counter_3_q[15:12]));  // open: load, up, count, D
  Counter #(.max('h2), .width(4)) counter_5 (
    .clr(and_1_out), .clk(counter_6_carry), .carry(counter_5_carry), .Q(counter_5_q));  // open: load, up, count, D
  or or_1 (or_1_out, and_1_out, counter_6_carry);
  Counter #(.max('ha), .width(4)) counter_6 (
    .clr(or_1_out), .clk(counter_3_carry), .carry(counter_6_carry), .Q(counter_6_q));  // open: load, up, count, D
  Comparator #(.width(4)) comparator_1 (.a(4'b0100), .b(counter_6_q), .eq(comparator_1_eq));  // open: gt, lt
  and and_1 (and_1_out, counter_5_carry, comparator_1_eq);
  Counter #(.max('h6), .width(4)) counter_7 (
    .clr(counter_7_carry), .clk(counter_8_carry), .carry(counter_7_carry), .Q(counter_7_q));  // open: load, up, count, D
  Counter #(.max('ha), .width(4)) counter_8 (
    .clr(counter_8_carry), .clk(set_hours), .carry(counter_8_carry), .Q(counter_8_q));  // open: load, up, count, D
  Register #(.width(4)) register_1 (.D(counter_8_q), .en(set_alarm), .clk(clock_1_out), .Q(register_1_q));  // open: clr
  Multiplexer #(.select(2), .width(16)) multiplexer_1 (
    .in0({counter_3_q, counter_6_q, counter_5_q}), .in1({register_1_q, register_2_q, register_3_q}),
    .out(output_time), .sel(select_inputs));  // open: in2, in3
  Counter #(.max('h2), .width(4)) counter_9 (
    .clr(and_2_out), .clk(counter_10_carry), .carry(counter_9_carry), .Q(counter_9_q));  // open: load, up, count, D
  or or_2 (or_2_out, and_2_out, counter_10_carry);
  Counter #(.max('ha), .width(4)) counter_10 (
    .clr(or_2_out), .clk(set_minutes), .carry(counter_10_carry), .Q(counter_10_q));  // open: load, up, count, D
  Register #(.width(4)) register_2 (.D(counter_7_q), .en(set_alarm), .clk(clock_1_out), .Q(register_2_q));  // open: clr
  Comparator #(.width(16)) comparator_2 (
    .a({register_1_q, register_2_q, register_3_q}), .b({counter_3_q, counter_6_q, counter_5_q}),
    .eq(alarm_signal));  // open: gt, lt
  Comparator #(.width(4)) comparator_3 (.a(4'b0100), .b(counter_10_q), .eq(comparator_3_eq));  // open: gt, lt
  Register #(.width(4)) register_3 (
    .D(counter_9_q), .en(set_alarm), .clk(clock_1_out), .Q(register_3_q[3:0]));  // open: clr
  and and_2 (and_2_out, counter_9_carry, comparator_3_eq);
  Register #(.width(4)) register_4 (
    .D(counter_10_q), .en(set_alarm), .clk(clock_1_out), .Q(register_3_q[7:4]));  // open: clr
endmodule

module display_clock (
  input  set_alarm,
  input  [1:0] select_inputs
);

  wire bcd_to_7_segment_decoder_1_p1, bcd_to_7_segment_decoder_1_p2, bcd_to_7_segment_decoder_1_p3,
       bcd_to_7_segment_decoder_1_p4, bcd_to_7_segment_decoder_1_p6, bcd_to_7_segment_decoder_1_p7,
       bcd_to_7_segment_decoder_1_p8, bcd_to_7_segment_decoder_2_p1, bcd_to_7_segment_decoder_2_p2,
       bcd_to_7_segment_decoder_2_p3, bcd_to_7_segment_decoder_2_p4, bcd_to_7_segment_decoder_2_p6,
       bcd_to_7_segment_decoder_2_p7, bcd_to_7_segment_decoder_2_p8, bcd_to_7_segment_decoder_3_p1,
       bcd_to_7_segment_decoder_3_p2, bcd_to_7_segment_decoder_3_p3, bcd_to_7_segment_decoder_3_p4,
       bcd_to_7_segment_decoder_3_p6, bcd_to_7_segment_decoder_3_p7, bcd_to_7_segment_decoder_3_p8,
       bcd_to_7_segment_decoder_4_p1, bcd_to_7_segment_decoder_4_p2, bcd_to_7_segment_decoder_4_p3,
       bcd_to_7_segment_decoder_4_p4, bcd_to_7_segment_decoder_4_p6, bcd_to_7_segment_decoder_4_p7,
       bcd_to_7_segment_decoder_4_p8, bcd_to_7_segment_decoder_5_p1, bcd_to_7_segment_decoder_5_p2,
       bcd_to_7_segment_decoder_5_p3, bcd_to_7_segment_decoder_5_p4, bcd_to_7_segment_decoder_5_p6,
       bcd_to_7_segment_decoder_5_p7, bcd_to_7_segment_decoder_5_p8, bcd_to_7_segment_decoder_6_p1,
       bcd_to_7_segment_decoder_6_p2, bcd_to_7_segment_decoder_6_p3, bcd_to_7_segment_decoder_6_p4,
       bcd_to_7_segment_decoder_6_p6, bcd_to_7_segment_decoder_6_p7, bcd_to_7_segment_decoder_6_p8,
       change_hours_out, change_minutes_out, clock_work_1_alarm_signal, not_1_out, not_2_out;
  wire [3:0] bcd_to_7_segment_decoder_1_p5, clock_work_1_output_time, clock_work_1_output_time_2,
       clock_work_1_seconds_0, clock_work_1_seconds_1, controlled_buffer_1_out, controlled_buffer_2_out;
  wire [7:4] bcd_to_7_segment_decoder_2_p5;

  Button change_hours (.out(change_hours_out));
  Button change_minutes (.out(change_minutes_out));
  // BCD_to_7_Segment_decoder bcd_to_7_segment_decoder_1: pin names not known; wires that end beside it: bcd_to_7_segment_decoder_1_p1, bcd_to_7_segment_decoder_1_p2, bcd_to_7_segment_decoder_1_p3, bcd_to_7_segment_decoder_1_p4, bcd_to_7_segment_decoder_1_p5, bcd_to_7_segment_decoder_1_p6, bcd_to_7_segment_decoder_1_p7, bcd_to_7_segment_decoder_1_p8
  _7_Segment_Display u_7_segment_display_1 (
    .g(bcd_to_7_segment_decoder_1_p1), .f(bcd_to_7_segment_decoder_1_p3), .a(bcd_to_7_segment_decoder_1_p6),
    .b(bcd_to_7_segment_decoder_1_p8), .e(bcd_to_7_segment_decoder_1_p2), .d(bcd_to_7_segment_decoder_1_p4),
    .c(bcd_to_7_segment_decoder_1_p7));  // open: dp
  // BCD_to_7_Segment_decoder bcd_to_7_segment_decoder_2: pin names not known; wires that end beside it: bcd_to_7_segment_decoder_2_p1, bcd_to_7_segment_decoder_2_p2, bcd_to_7_segment_decoder_2_p3, bcd_to_7_segment_decoder_2_p4, bcd_to_7_segment_decoder_2_p5, bcd_to_7_segment_decoder_2_p6, bcd_to_7_segment_decoder_2_p7, bcd_to_7_segment_decoder_2_p8
  _7_Segment_Display u_7_segment_display_2 (
    .g(bcd_to_7_segment_decoder_2_p1), .f(bcd_to_7_segment_decoder_2_p3), .a(bcd_to_7_segment_decoder_2_p6),
    .b(bcd_to_7_segment_decoder_2_p8), .e(bcd_to_7_segment_decoder_2_p2), .d(bcd_to_7_segment_decoder_2_p4),
    .c(bcd_to_7_segment_decoder_2_p7));  // open: dp
  clock_work clock_work_1 (
    .set_minutes(change_hours_out), .set_hours(change_minutes_out), .set_alarm(set_alarm),
    .select_inputs(select_inputs), .seconds_1(clock_work_1_seconds_1), .seconds_0(clock_work_1_seconds_0),
    .alarm_signal(clock_work_1_alarm_signal),
    .output_time({clock_work_1_output_time_2, clock_work_1_output_time, bcd_to_7_segment_decoder_2_p5, bcd_to_7_segment_decoder_1_p5}));
  not not_1 (not_1_out, set_alarm);
  not not_2 (not_2_out, set_alarm);
  // BCD_to_7_Segment_decoder bcd_to_7_segment_decoder_3: pin names not known; wires that end beside it: bcd_to_7_segment_decoder_3_p1, bcd_to_7_segment_decoder_3_p2, bcd_to_7_segment_decoder_3_p3, bcd_to_7_segment_decoder_3_p4, clock_work_1_output_time, bcd_to_7_segment_decoder_3_p6, bcd_to_7_segment_decoder_3_p7, bcd_to_7_segment_decoder_3_p8
  _7_Segment_Display u_7_segment_display_3 (
    .g(bcd_to_7_segment_decoder_3_p1), .f(bcd_to_7_segment_decoder_3_p3), .a(bcd_to_7_segment_decoder_3_p6),
    .b(bcd_to_7_segment_decoder_3_p8), .e(bcd_to_7_segment_decoder_3_p2), .d(bcd_to_7_segment_decoder_3_p4),
    .c(bcd_to_7_segment_decoder_3_p7));  // open: dp
  assign controlled_buffer_1_out = not_1_out ? clock_work_1_seconds_0 : 4'bz;  // Controlled_Buffer controlled_buffer_1
  assign controlled_buffer_2_out = not_2_out ? clock_work_1_seconds_1 : 4'bz;  // Controlled_Buffer controlled_buffer_2
  // BCD_to_7_Segment_decoder bcd_to_7_segment_decoder_4: pin names not known; wires that end beside it: bcd_to_7_segment_decoder_4_p1, bcd_to_7_segment_decoder_4_p2, bcd_to_7_segment_decoder_4_p3, bcd_to_7_segment_decoder_4_p4, clock_work_1_output_time_2, bcd_to_7_segment_decoder_4_p6, bcd_to_7_segment_decoder_4_p7, bcd_to_7_segment_decoder_4_p8
  _7_Segment_Display u_7_segment_display_4 (
    .g(bcd_to_7_segment_decoder_4_p1), .f(bcd_to_7_segment_decoder_4_p3), .a(bcd_to_7_segment_decoder_4_p6),
    .b(bcd_to_7_segment_decoder_4_p8), .e(bcd_to_7_segment_decoder_4_p2), .d(bcd_to_7_segment_decoder_4_p4),
    .c(bcd_to_7_segment_decoder_4_p7));  // open: dp
  // BCD_to_7_Segment_decoder bcd_to_7_segment_decoder_5: pin names not known; wires that end beside it: bcd_to_7_segment_decoder_5_p1, bcd_to_7_segment_decoder_5_p2, bcd_to_7_segment_decoder_5_p3, bcd_to_7_segment_decoder_5_p4, controlled_buffer_2_out, bcd_to_7_segment_decoder_5_p6, bcd_to_7_segment_decoder_5_p7, bcd_to_7_segment_decoder_5_p8
  _7_Segment_Display u_7_segment_display_5 (
    .g(bcd_to_7_segment_decoder_5_p1), .f(bcd_to_7_segment_decoder_5_p3), .a(bcd_to_7_segment_decoder_5_p6),
    .b(bcd_to_7_segment_decoder_5_p8), .e(bcd_to_7_segment_decoder_5_p2), .d(bcd_to_7_segment_decoder_5_p4),
    .c(bcd_to_7_segment_decoder_5_p7));  // open: dp
  LED ALARM (.in(clock_work_1_alarm_signal));
  // BCD_to_7_Segment_decoder bcd_to_7_segment_decoder_6: pin names not known; wires that end beside it: bcd_to_7_segment_decoder_6_p1, bcd_to_7_segment_decoder_6_p2, bcd_to_7_segment_decoder_6_p3, bcd_to_7_segment_decoder_6_p4, controlled_buffer_1_out, bcd_to_7_segment_decoder_6_p6, bcd_to_7_segment_decoder_6_p7, bcd_to_7_segment_decoder_6_p8
  _7_Segment_Display u_7_segment_display_6 (
    .g(bcd_to_7_segment_decoder_6_p1), .f(bcd_to_7_segment_decoder_6_p3), .a(bcd_to_7_segment_decoder_6_p6),
    .b(bcd_to_7_segment_decoder_6_p8), .e(bcd_to_7_segment_decoder_6_p2), .d(bcd_to_7_segment_decoder_6_p4),
    .c(bcd_to_7_segment_decoder_6_p7));  // open: dp

  // Notes on the sheet:
  //   Set this input to 1 to change the alarm time
  //   Settings for the hours and minutes of the alarm clock time
  //   Set this input to 00 to display the clock
  //   Set this input to 01 to view the alarm time
  //   Alarm Indicator
endmodule
